# Fritzing sketch keke (saved by Fritzing 0.9.3b)
stripboards: 1

parts:
  Composant1 = Arduino Nano (Rev3.0)
  Composant2 = Bluetooth HC-05 Macho
  Q1 = MOSFET-NCHANNEL [package=to220v]
  Q2 = MOSFET-NCHANNEL [package=to220v]
  D1 = Rectifier Diode [part_number=1N4001 package="300 mil [THT]"]
  R1 = Resistor [tolerance=±5% resistance=220 package=THT]
  R2 = Resistor [tolerance=±5% resistance=220 package=THT]
  J1 = female pin header, 1 pin [form="♀ (female)"]
  J3 = female pin header, 1 pin [form="♀ (female)"]
  J4 = female pin header, 1 pin [form="♀ (female)"]
  J5 = female pin header, 1 pin [form="♀ (female)"]
  R4 = Resistor [tolerance=±5% resistance=10k package=THT]
  R5 = Resistor [tolerance=±5% resistance=10k package=THT]
  R6 = Resistor [tolerance=±5% resistance=10k package=THT]
  R7 = Resistor [tolerance=±5% resistance=20k package=THT]
  R8 = Resistor [tolerance=±5% resistance=10k package=THT]

nets:
  N1: Composant1.D1/TX, R6.Pin_1
  N2: Composant1.D0/RX, Composant2.RXD
  GND: Composant1.GND, Composant2.GND, Q1.S, Q2.S, R4.Pin_0, R5.Pin_0, R7.Pin_0
  N3: Composant1.D4, R1.Pin_0
  N4: Composant1.D5, R2.Pin_0
  11.3V: Composant1.VIN, D1.cathode
  3.3V: Composant1.3V3, Composant2.VCC
  N5: Q1.G, R1.Pin_1, R5.Pin_1
  N6: Q1.D, J5.pin1, R8.Pin_0
  N7: Q2.G, R2.Pin_1, R4.Pin_1
  N8: Q2.D, J4.pin1
  12V: D1.anode, J1.pin1, J3.pin1, R8.Pin_1
  N9: R6.Pin_0, R7.Pin_1

notes:
  DreamCar
  12V_batt
  GND_batt
  GND_mot
  control_mot
  12V_mot
